# Fritzing sketch bot (saved by Fritzing 0.9.6b)

parts:
  U1 = ESP8266 NodeMCU LoLin module
  HC-SR04_Sensor_1 = HC-SR04 Ultrasonic Distance Sensor
  M1 = gear-motor
  M2 = gear-motor
  VCC1 = 4 x AAA Battery Mount
  U2 = L9110 H-bridge module [part_number="L9110 H-bridge"]

nets:
  N1: U1.D0, U2.B-IB
  N2: U1.D1, U2.A-IB
  N3: U1.D5, U2.B-IA
  N4: U1.D6, HC-SR04_Sensor_1.TRIG, HC-SR04_Sensor_1.ECHO
  N5: U1.D7, U2.A-IA
  VCC: U1.Vin, HC-SR04_Sensor_1.VCC, VCC1.+, U2.VCC
  N6: M1.pin_1, U2.MOTOR_A-B
  N7: M1.pin_2, U2.MOTOR_A-A
  N8: M2.pin_1, U2.MOTOR_B-B
  N9: M2.pin_2, U2.MOTOR_B-A

custom parts:
  ESP8266 NodeMCU LoLin module: ESP8266 based NodeMCU
